// Logisim project ALU.circ as structural Verilog: 1 circuit, main circuit ALU
// LAB12-ALU
module ALU (
  input  [31:0] ALU_Source_1,
  input  [31:0] ALU_Source_2,
  input  [2:0] ALU_Control,
  output [31:0] ALU_Result
);

  wire [4:0] bit_extender_1_out, bit_extender_2_out;
  wire [31:0] adder_1_out, and_1_out, multiplier_1_out, or_1_out, shifter_1_out, shifter_2_out,
       subtractor_1_out, xor_1_out;

  // Probe on ALU_Source_1
  // Probe on ALU_Source_2
  assign and_1_out = ALU_Source_1 & ALU_Source_2;  // AND_Gate and_1, 32 bits wide
  assign or_1_out = ALU_Source_1 | ALU_Source_2;  // OR_Gate or_1, 32 bits wide
  assign xor_1_out = ALU_Source_1 ^ ALU_Source_2;  // XOR_Gate xor_1, 32 bits wide
  Bit_Extender #(.in_width(32), .out_width(5)) bit_extender_1 (.in(ALU_Source_2), .out(bit_extender_1_out));
  Bit_Extender #(.in_width(32), .out_width(5)) bit_extender_2 (.in(ALU_Source_2), .out(bit_extender_2_out));
  Adder #(.width(32)) adder_1 (.a(ALU_Source_1), .b(ALU_Source_2), .out(adder_1_out));  // open: cin, cout
  Subtractor #(.width(32)) subtractor_1 (
    .a(ALU_Source_1), .b(ALU_Source_2), .out(subtractor_1_out));  // open: bin, bout
  Shifter #(.width(32)) shifter_1 (.in(ALU_Source_1), .\dist (bit_extender_1_out), .out(shifter_1_out));
  Shifter #(.width(32), .shift("lr")) shifter_2 (.in(ALU_Source_1), .\dist (bit_extender_2_out), .out(shifter_2_out));
  Multiplexer #(.select(3), .width(32)) multiplexer_1 (
    .in0(shifter_1_out), .in1(shifter_2_out), .in2(adder_1_out), .in3(subtractor_1_out),
    .in4(multiplier_1_out), .in5(and_1_out), .in6(or_1_out), .in7(xor_1_out), .out(ALU_Result),
    .sel(ALU_Control));  // open: en
  Multiplier #(.width(32)) multiplier_1 (
    .a(ALU_Source_1), .b(ALU_Source_2), .out(multiplier_1_out));  // open: cin, cout
  // Probe on ALU_Result

  // Other names for the same wires on the sheet: control[2:0] = ALU_Control; result[31:0] = ALU_Result;
  //   source1[31:0] = ALU_Source_1; source2[31:0] = ALU_Source_2

  // Notes on the sheet:
  //   DO NOT CROSS WIRES
  //   OVER THIS BOX
  //   DO NOT CROSS WIRES
  //   OVER THIS BOX
  //   COMPUTE ALL POSSIBLE OPERATIONS
  //   DO NOT CROSS WIRES
  //   OVER THIS BOX
  //   DO NOT CROSS WIRES
  //   OVER THIS BOX
endmodule
