// Logisim project fib.circ as structural Verilog: 1 circuit, main circuit main
module main (
  input  [9:0] in_1,
  output [9:0] out_2
);

  wire clock_1_out, comparator_1_eq, comparator_2_eq, not_1_out;
  wire [9:0] adder_1_out, counter_1_q, multiplexer_1_out, register_1_q;

  Clock clock_1 (.out(clock_1_out));
  Register #(.width(10)) register_1 (.D(out_2), .en(not_1_out), .Q(register_1_q), .clk(clock_1_out));  // open: clr
  Adder #(.width(10)) adder_1 (.a(register_1_q), .b(multiplexer_1_out), .out(adder_1_out));  // open: cin, cout
  Counter #(.width(10), .max('h3ff)) counter_1 (
    .count(not_1_out), .Q(counter_1_q), .clk(clock_1_out));  // open: load, D, carry, clr
  Register #(.width(10)) register_2 (.D(adder_1_out), .en(not_1_out), .Q(out_2), .clk(clock_1_out));  // open: clr
  Comparator #(.width(10)) comparator_1 (.a(counter_1_q), .b(in_1), .eq(comparator_1_eq));  // open: gt, lt
  not not_1 (not_1_out, comparator_1_eq);
  // Probe on in_1
  // Probe on out_2
  // Probe on register_1_q
  Multiplexer #(.width(10), .enable("false")) multiplexer_1 (
    .in0(out_2), .in1(10'h1), .out(multiplexer_1_out), .sel(comparator_2_eq));
  Comparator #(.width(10)) comparator_2 (.a(out_2), .b({10{1'b0}}), .eq(comparator_2_eq));  // open: gt, lt
endmodule
