// Logisim project alu.circ as structural Verilog: 1 circuit, main circuit main
module main (
  input  [31:0] X,
  input  [31:0] Y,
  input  [5:0] Switch__S,
  input  [3:0] in_4,
  input  [7:0] in_5,
  input  [3:0] in_6,
  input  [2:0] in_7,
  output Signed_Overflow,
  output [31:0] RESULT,
  output Equal,
  output [3:0] out,
  output [7:0] out_2
);

  wire addOverflow, and_2_out, and_3_out, and_4_out, and_5_out, and_6_out, and_7_out, and_8_out, and_9_out,
       comparator_1_lt, comparator_2_lt, comparator_3_eq, comparator_4_eq, comparator_4_gt, comparator_4_lt,
       comparator_5_eq, comparator_5_gt, comparator_5_lt, comparator_7_eq, comparator_7_gt, comparator_8_eq,
       comparator_8_gt, decoder_1_out0, decoder_1_out2, not_1_out, or_2_out, or_3_out, or_4_out, or_5_out,
       or_6_out, or_7_out, or_9_out, subOverflow, xltz, xor_1_out, xor_3_out, yltz;
  wire [1:0] bit_extender_5_out;
  wire [4:0] y5;
  wire [31:0] addOut, andOut, bitpalOut, lfsrOut, orOut, sllOut, sltOut, sltuOut, sraOut, srlOut, subOut;
  wire [31:31] shifter_1_out;

  // Probe on in_4
  // Probe on in_6
  Bit_Extender #(.in_width(32), .out_width(5)) bit_extender_1 (.in(Y), .out(y5));
  Shifter #(.width(32), .shift("lr")) shifter_1 (.in(X), .\dist (5'b00001), .out({shifter_1_out[31], lfsrOut[30:0]}));
  Subtractor #(.width(4)) subtractor_1 (.a(in_4), .b(in_6), .out(out));  // open: bin, bout
  // Probe on X
  // Probe on Y
  // Probe on out
  Shifter #(.width(32)) shifter_2 (.in(X), .\dist (y5), .out(sllOut));
  Shifter #(.width(32), .shift("lr")) shifter_3 (.in(X), .\dist (y5), .out(srlOut));
  Shifter #(.width(32), .shift("ar")) shifter_4 (.in(X), .\dist (y5), .out(sraOut));
  xor xor_1 (xor_1_out, X[0], X[2]);
  xor xor_2 (lfsrOut[31], xor_3_out, X[5]);
  xor xor_3 (xor_3_out, xor_1_out, X[3]);
  Adder #(.width(32)) adder_1 (.a(X), .b(Y), .out(addOut));  // open: cin, cout
  Subtractor #(.width(32)) subtractor_2 (.a(X), .b(Y), .out(subOut));  // open: bin, bout
  assign andOut = X & Y;  // AND_Gate and_1, 32 bits wide
  assign orOut = X | Y;  // OR_Gate or_1, 32 bits wide
  Comparator #(.width(32)) comparator_1 (.a(X), .b(Y), .lt(comparator_1_lt));  // open: gt, eq
  Comparator #(.width(32), .mode("unsigned")) comparator_2 (.a(X), .b(Y), .lt(comparator_2_lt));  // open: gt, eq
  Shifter #(.shift("rr")) shifter_5 (.in(in_5), .\dist (in_7), .out(out_2));
  assign sltOut = {{31{1'b0}}, comparator_1_lt};  // Bit_Extender bit_extender_2
  assign sltuOut = {{31{1'b0}}, comparator_2_lt};  // Bit_Extender bit_extender_3
  Comparator #(.width(16), .mode("unsigned")) comparator_3 (
    .a({X[0], X[1], X[2], X[3], X[4], X[5], X[6], X[7], X[8], X[9], X[10], X[11], X[12], X[13], X[14], X[15]}),
    .b(X[31:16]), .eq(comparator_3_eq));  // open: gt, lt
  assign bitpalOut = {{31{1'b0}}, comparator_3_eq};  // Bit_Extender bit_extender_4
  Comparator #(.width(32)) comparator_4 (
    .a(addOut), .b({32{1'b0}}), .gt(comparator_4_gt), .eq(comparator_4_eq), .lt(comparator_4_lt));
  Comparator #(.width(32)) comparator_5 (
    .a(subOut), .b({32{1'b0}}), .gt(comparator_5_gt), .eq(comparator_5_eq), .lt(comparator_5_lt));
  Multiplexer #(.select(5), .width(32), .enable("false")) multiplexer_1 (
    .in0(sllOut), .in2(srlOut), .in3(sraOut), .in16(addOut), .in17(addOut), .in18(subOut), .in19(subOut),
    .in20(andOut), .in21(orOut), .in26(sltOut), .in27(sltuOut), .in30(bitpalOut), .in31(lfsrOut),
    .out(RESULT), .sel({Switch__S[5], Switch__S[3:0]}));  // open: in1, in4, in5, in6, in7, in8, in9, in10, in11, in12, in13, in14, in15, in22, in23, in24, in25, in28, in29
  or or_2 (or_2_out, comparator_4_gt, comparator_4_eq);
  and and_2 (and_2_out, comparator_4_lt, or_6_out);
  or or_3 (or_3_out, comparator_5_gt, comparator_5_eq);
  and and_3 (and_3_out, yltz, comparator_5_lt);
  Comparator #(.width(32), .mode("unsigned")) comparator_6 (.a(X), .b(Y), .eq(Equal));  // open: gt, lt
  Comparator #(.width(32)) comparator_7 (.a(X), .b({32{1'b0}}), .gt(comparator_7_gt), .eq(comparator_7_eq), .lt(xltz));
  Comparator #(.width(32)) comparator_8 (.a(Y), .b({32{1'b0}}), .gt(comparator_8_gt), .eq(comparator_8_eq), .lt(yltz));
  and and_4 (and_4_out, yltz, or_2_out);
  Bit_Extender #(.in_width(6), .out_width(2)) bit_extender_5 (.in(Switch__S), .out(bit_extender_5_out));
  or or_4 (or_4_out, and_4_out, and_2_out);
  and and_5 (and_5_out, or_6_out, or_3_out);
  Decoder #(.select(2), .enable("false")) decoder_1 (
    .out0(decoder_1_out0), .out2(decoder_1_out2), .sel(bit_extender_5_out));  // open: out1, out3
  // Probe on RESULT
  or or_5 (or_5_out, comparator_7_gt, comparator_7_eq);
  or or_6 (or_6_out, comparator_8_gt, comparator_8_eq);
  and and_6 (and_6_out, xltz, yltz);
  or or_7 (or_7_out, and_5_out, and_3_out);
  and and_7 (and_7_out, decoder_1_out2, subOverflow);
  or or_8 (Signed_Overflow, and_7_out, and_9_out);
  and and_8 (and_8_out, or_5_out, or_6_out);
  and and_9 (and_9_out, decoder_1_out0, addOverflow);
  or or_9 (or_9_out, and_8_out, and_6_out);
  not not_1 (not_1_out, or_9_out);
  and and_10 (addOverflow, or_9_out, or_4_out);
  and and_11 (subOverflow, not_1_out, or_7_out);

  // Other names for the same wires on the sheet: sw[5:0] = Switch__S

  // Notes on the sheet:
  //   INPUTS to your circuit
  //   INPUT to your circuit
  //   DON'T CHANGE THE INPUTS AND OUTPUTS! IF YOU DO SO, YOU NEED TO MAKE SURE THE PINS ARE IN THE RIGHT PLACES!
  //   OUTPUTS of your circuit
  //   sign of addOut and y is different
  //   subOut and y have same sign
  //   x and y have same sign
endmodule
