// Logisim project cpu.circ as structural Verilog: 4 circuits, main circuit main
module main (
  input  [31:0] RS_READ_VALUE,
  input  [31:0] RT_READ_VALUE,
  input  [31:0] INSTRUCTION,
  input  CLOCK,
  input  RESET,
  output [31:0] t0,
  output [31:0] t1,
  output [31:0] t2,
  output [31:0] t3,
  output [4:0] RS,
  output [4:0] RT,
  output [4:0] Write_Register,
  output [31:0] RD_WRITE_VALUE,
  output RD_WRITE_ENABLE,
  output [23:0] FETCH_ADDRESS
);

  wire accessByte, ALUOp0, ALUOp1, ALUSrc, and_1_out, and_2_out, and_3_out, Branch, branchNE, equal,
       instRDInRange, instRSInRange, instRTInRange, jal, Jump, jumpReg, MemRead, MemtoReg, MemWrite,
       not_1_out, or_1_out, overflow, RegDst, shift, upperLoad;
  wire [1:0] instRD2, instRS2, instRT2;
  wire [4:0] instRD;
  wire [5:0] ALUCO, funct;
  wire [31:0] adder_2_out, ALU_result, ALUx, ALUy, bit_extender_2_out, immdt, MEM_data_mem_out, memData,
       multiplexer_3_out, multiplexer_4_out, multiplexer_9_out, multiplexer_10_out, multiplexer_11_out, PC,
       PCinc, rsData, rsData2, rtData, rtData2, shifter_1_out;

  Multiplexer #(.width(5), .enable("false")) multiplexer_1 (
    .in0(instRD), .in1({5{1'b1}}), .out(Write_Register), .sel(jal));
  Multiplexer #(.width(32), .enable("false")) multiplexer_2 (
    .in0(memData), .in1(PCinc), .out(RD_WRITE_VALUE), .sel(jal));
  Bit_Extender #(.in_width(32), .out_width(24)) bit_extender_1 (.in(PC), .out(FETCH_ADDRESS));
  Multiplexer #(.width(32), .enable("false")) multiplexer_3 (
    .in0(rtData), .in1(immdt), .out(multiplexer_3_out), .sel(ALUSrc));
  assign bit_extender_2_out = {{27{1'b0}}, INSTRUCTION[10:6]};  // Bit_Extender bit_extender_2
  Shifter #(.width(32)) shifter_1 (.in(immdt), .\dist (5'b10000), .out(shifter_1_out));
  Bit_Extender #(.in_width(16), .out_width(6)) bit_extender_3 (.in(INSTRUCTION[15:0]), .out(funct));
  Multiplexer #(.width(32), .enable("false")) multiplexer_4 (
    .in0(multiplexer_3_out), .in1(bit_extender_2_out), .out(multiplexer_4_out), .sel(shift));
  // Probe on ALUy
  Multiplexer #(.width(32), .enable("false")) multiplexer_5 (
    .in0(multiplexer_4_out), .in1(shifter_1_out), .out(ALUy), .sel(upperLoad));
  // Probe on instRD2
  // Probe on memData
  // Probe on ALU_result
  // Probe on ALUx
  assign immdt = {{16{INSTRUCTION[15]}}, INSTRUCTION[15:0]};  // Bit_Extender bit_extender_4
  ALUControl alucontrol_1 (.ALUOp0(ALUOp0), .ALUOp1(ALUOp1), .funct(funct), .ALU_out(ALUCO));
  Multiplexer #(.width(32), .enable("false")) multiplexer_6 (.in0(rsData), .in1(rtData), .out(ALUx), .sel(shift));
  alu_main ALU (.Switch__S(ALUCO), .X(ALUx), .Equal(equal), .RESULT(ALU_result), .Signed_Overflow(overflow), .Y(ALUy));
  Multiplexer #(.width(5), .enable("false")) multiplexer_7 (
    .in0(INSTRUCTION[20:16]), .in1(INSTRUCTION[15:11]), .out(instRD), .sel(RegDst));
  regfile_main RegFile (
    .Read_register_1(instRS2), .Read_register_2(instRT2), .write_register(instRD2), .write_data(memData),
    .t0_Value(t0), .t1_Value(t1), .t2_Value(t2), .t3_Value(t3), .RegWrite(and_1_out), .clock(CLOCK),
    .Read_Data_1(rsData2), .Read_Data_2(rtData2));
  and and_1 (and_1_out, RD_WRITE_ENABLE, instRDInRange);
  mem_main MEM (
    .Data_Mem_Addr(ALU_result), .Data_Mem_In(rtData), .ACCESS_BYTE(accessByte), .MEM_WRITE(MemWrite),
    .CLOCK(CLOCK), .Data_Mem_Out(MEM_data_mem_out));
  Multiplexer #(.width(32), .enable("false")) multiplexer_8 (
    .in0(ALU_result), .in1(MEM_data_mem_out), .out(memData), .sel(MemtoReg));
  Register #(.width(32)) register_1 (.D(multiplexer_11_out), .Q(PC), .clk(CLOCK));  // open: en, clr
  ControlUnit controlunit_1 (
    .opcode(INSTRUCTION[31:26]), .funct(funct), .RegDst(RegDst), .Branch(Branch), .MemRead(MemRead),
    .MemToReg(MemtoReg), .MemWrite(MemWrite), .ALUSrc(ALUSrc), .RegWrite(RD_WRITE_ENABLE), .Jump(Jump),
    .ALUOp0(ALUOp0), .ALUOp1(ALUOp1), .shift(shift), .accessByte(accessByte), .upperLoad(upperLoad),
    .branchNE(branchNE), .jumpReg(jumpReg), .jal(jal));
  Adder #(.width(32)) adder_1 (.a(PC), .b(32'h1), .out(PCinc));  // open: cin, cout
  Adder #(.width(32)) adder_2 (.a(PCinc), .b(immdt), .out(adder_2_out));  // open: cin, cout
  not not_1 (not_1_out, equal);
  Multiplexer #(.width(32), .enable("false")) multiplexer_9 (
    .in0(PCinc), .in1(adder_2_out), .out(multiplexer_9_out), .sel(or_1_out));
  and and_2 (and_2_out, Branch, equal);
  and and_3 (and_3_out, branchNE, not_1_out);
  or or_1 (or_1_out, and_2_out, and_3_out);
  Multiplexer #(.width(32), .enable("false")) multiplexer_10 (
    .in0(multiplexer_9_out), .in1(immdt), .out(multiplexer_10_out), .sel(Jump));
  Multiplexer #(.width(32), .enable("false")) multiplexer_11 (
    .in0(multiplexer_10_out), .in1(rsData), .out(multiplexer_11_out), .sel(jumpReg));
  Multiplexer #(.width(32), .enable("false")) multiplexer_12 (
    .in0(RS_READ_VALUE), .in1(rsData2), .out(rsData), .sel(instRSInRange));
  Multiplexer #(.width(32), .enable("false")) multiplexer_13 (
    .in0(RT_READ_VALUE), .in1(rtData2), .out(rtData), .sel(instRTInRange));
  RegControl regcontrol_1 (.Register(INSTRUCTION[25:21]), .translatedReg(instRS2), .inRange(instRSInRange));
  RegControl regcontrol_2 (.Register(INSTRUCTION[20:16]), .translatedReg(instRT2), .inRange(instRTInRange));
  RegControl regcontrol_3 (.Register(instRD), .translatedReg(instRD2), .inRange(instRDInRange));

  assign RS = INSTRUCTION[25:21];
  assign RT = INSTRUCTION[20:16];

  // Other names for the same wires on the sheet: CLK = CLOCK; shamt[4:0] = INSTRUCTION[10:6];
  //   instRT[4:0] = INSTRUCTION[20:16]; instRS[4:0] = INSTRUCTION[25:21]; opcode[5:0] = INSTRUCTION[31:26];
  //   RegWrite = RD_WRITE_ENABLE; rsData1[31:0] = RS_READ_VALUE; rtData1[31:0] = RT_READ_VALUE

  // Notes on the sheet:
  //   These are outputs/inputs from run.circ
  //   These are outputs to run.circ
endmodule

module ControlUnit (
  input  [5:0] opcode,
  input  [5:0] funct,
  output RegDst,
  output Branch,
  output MemRead,
  output MemToReg,
  output MemWrite,
  output ALUSrc,
  output RegWrite,
  output Jump,
  output ALUOp0,
  output ALUOp1,
  output shift,
  output accessByte,
  output upperLoad,
  output branchNE,
  output jumpReg,
  output jal
);

  wire and_3_out, and_4_out, and_6_out, and_13_out, and_14_out, and_15_out, and_16_out, ori;

  and and_1 (shift, and_4_out, RegDst);
  and and_2 (RegDst, ~opcode[5], ~opcode[4], ~opcode[3], ~opcode[2], ~opcode[1], ~opcode[0]);  // AND_Gate
  and and_3 (and_3_out, ~opcode[5], ~opcode[4], ~opcode[3], ~opcode[2], opcode[1]);  // AND_Gate
  or or_1 (Jump, jumpReg, and_3_out);
  and and_4 (and_4_out, ~funct[5], ~funct[4], ~funct[3], ~funct[2]);  // AND_Gate
  and and_5 (Branch, ~opcode[5], ~opcode[4], ~opcode[3], opcode[2], ~opcode[1]);  // AND_Gate
  and and_6 (and_6_out, ~funct[5], ~funct[4], funct[3], ~funct[2], ~funct[1], ~funct[0]);  // AND_Gate
  and and_7 (MemRead, opcode[5], ~opcode[3]);  // AND_Gate
  and and_8 (ALUSrc, ~RegDst, ~Branch);  // AND_Gate
  and and_9 (jumpReg, and_6_out, RegDst);
  and and_10 (MemWrite, opcode[5], ~opcode[4], opcode[3], ~opcode[2], opcode[1], opcode[0]);  // AND_Gate
  and and_11 (jal, ~opcode[5], ~opcode[4], ~opcode[3], ~opcode[2], opcode[1], opcode[0]);  // AND_Gate
  and and_12 (ori, ~opcode[5], ~opcode[4], opcode[3], opcode[2], ~opcode[1], opcode[0]);  // AND_Gate
  and and_13 (and_13_out, ~MemWrite, ~Branch, ~Jump);  // AND_Gate
  or or_2 (RegWrite, RegDst, jal, and_13_out);
  and and_14 (and_14_out, ~opcode[5], ~opcode[4], opcode[3], ~opcode[2], ~opcode[1], opcode[0]);  // AND_Gate
  and and_15 (and_15_out, ~opcode[5], opcode[4], ~opcode[3], ~opcode[2], opcode[1], ~opcode[0]);  // AND_Gate
  and and_16 (and_16_out, ~opcode[5], opcode[4], ~opcode[3], ~opcode[2], opcode[1], opcode[0]);  // AND_Gate
  or or_3 (ALUOp0, MemRead, and_14_out, ori, upperLoad, and_16_out);
  or or_4 (ALUOp1, and_15_out, ori, and_16_out);
  and and_17 (accessByte, opcode[5], ~opcode[4], ~opcode[3], ~opcode[1], ~opcode[0]);  // AND_Gate
  and and_18 (upperLoad, ~opcode[5], ~opcode[4], opcode[3], opcode[2], opcode[1], opcode[0]);  // AND_Gate
  and and_19 (branchNE, ~opcode[5], ~opcode[4], ~opcode[3], opcode[2], ~opcode[1], opcode[0]);  // AND_Gate

  assign MemToReg = MemRead;

  // Other names for the same wires on the sheet: rInstr = RegDst
endmodule

module RegControl (
  input  [4:0] Register,
  output [1:0] translatedReg,
  output inRange
);

  and and_1 (inRange, ~Register[2], Register[3], ~Register[4]);  // AND_Gate

  assign translatedReg = Register[1:0];
endmodule

module ALUControl (
  input  ALUOp0,
  input  ALUOp1,
  input  [5:0] funct,
  output [5:0] ALU_out
);

  wire and_2_out;
  wire [0:0] and_1_out;

  and and_1 (and_1_out[0], ALUOp1, ALUOp0);
  and and_2 (and_2_out, ~ALUOp0, ~ALUOp1);  // AND_Gate
  Multiplexer #(.width(6), .enable("false")) multiplexer_1 (
    .in0({3'b100, ALUOp1, 1'b0, and_1_out[0]}), .in1(funct), .out(ALU_out), .sel(and_2_out));
endmodule
